# Fritzing sketch 201 (saved by Fritzing 0.9.6b)

parts:
  R1 = Resistor [tolerance=±5% resistance=10000 package="0603 [SMD]"]
  R2 = Resistor [tolerance=±5% resistance=10000 package="0603 [SMD]"]
  R3 = Resistor [tolerance=±5% resistance=10000 package="0603 [SMD]"]
  Q1 = TIP120 Hi-Current Darlington Transistor  # not connected
  Q2 = TIP120 Hi-Current Darlington Transistor  # not connected
  Q3 = TIP120 Hi-Current Darlington Transistor  # not connected
  Mod1 = Heltec WiFi LoRa 32 V2 [part_number=HTIT-WB32LA]
  Power_plug1 = Power plug  # not connected

nets:
  N1: R1.Pin_0, Mod1.pin_8
  N2: R2.Pin_0, Mod1.pin_7
  N3: R3.Pin_0, Mod1.pin_6
