# Fritzing sketch Untitled Sketch 2 (saved by Fritzing 0.9.6b)
breadboards: 1

parts:
  LED1 = smd LED [color="Red (633nm)" package="0805 [SMD]"]
  R1 = Resistor [tolerance=±5% resistance=220 package="2512 [SMD]"]
  U1 = ESP32-38PinWide [part_number=ESP32-38PinWide]

nets:
  N1: LED1.cathode, U1.GPIO11
  N2: LED1.anode, R1.Pin_0
  N3: R1.Pin_1, U1.GPIO18

custom parts:
  ESP32-38PinWide: Generic 38-Pin ESP32 with wide format (only access to one side of pins on a breadboard) based on Stephen Lilley's HiLetgo ESP-WROOM-32 ESP32 ESP-32S Development Board.
