# Fritzing sketch 153 (saved by Fritzing 0.9.6b)
breadboards: 1

parts:
  DHT1 = DHT11 Humitidy and Temperature Sensor
  U1 = ESP32-38PinWide [part_number=ESP32-38PinWide]
  A1 = MQ-2 breakout  # not connected
  A2 = MQ-2 breakout  # not connected

nets:
  N1: DHT1.VDD, U1.GPIO11
  N2: DHT1.DATA, U1.GPIO12
  N3: DHT1.NULL, U1.VIN

custom parts:
  DHT11 Humitidy and Temperature Sensor: DHT11 Humidity and Temperature Sensor
  ESP32-38PinWide: Generic 38-Pin ESP32 with wide format (only access to one side of pins on a breadboard) based on Stephen Lilley's HiLetgo ESP-WROOM-32 ESP32 ESP-32S Development Board.
  MQ-2 breakout: MQ-2 gas sensor
