# Fritzing sketch 154 (saved by Fritzing 0.9.6b)

parts:
  Part1 = LCD1602-I2C
  U1 = ESP32-38PinWide [part_number=ESP32-38PinWide]

nets:
  N1: Part1.GND, U1.GPIO10, U1.GPIO11
  VCC: Part1.VCC, U1.VIN
  N2: Part1.SDA, U1.GPIO23, U1.GND
  N3: Part1.SCL, U1.GPIO18

custom parts:
  LCD1602-I2C: A standard character display, usually with 2x16 characters. Comes in many colors with LCM1602 IIC attached.
  ESP32-38PinWide: Generic 38-Pin ESP32 with wide format (only access to one side of pins on a breadboard) based on Stephen Lilley's HiLetgo ESP-WROOM-32 ESP32 ESP-32S Development Board.
